// Logisim project DM-02.circ as structural Verilog: 9 circuits, main circuit DM-02
module DM_02 (
  input  [7:0] in_1,
  input  [4:0] Function,
  input  in_3,
  input  in_4,
  input  in_5,
  input  in_6,
  input  in_7,
  input  in_8,
  input  in_9,
  input  in_10,
  input  in_11,
  input  in_12,
  input  in_13,
  input  in_14,
  input  in_15,
  input  in_16,
  input  in_17,
  input  in_18,
  input  in_19,
  input  in_20,
  input  in_21,
  input  in_22,
  input  in_23,
  input  in_24,
  input  in_25,
  input  in_26,
  input  in_27,
  input  in_28,
  input  in_29,
  input  in_30,
  input  in_31,
  input  in_32,
  input  in_33,
  input  in_34,
  input  in_35,
  output [4:0] FLAGS__DNZOC
);

  wire A_clock, ALU_clock, and_1_out, and_3_out, and_5_out, B_clock, C_clock, CLOCK1, CLOCK2, clock_1_out,
       H_clock, IR_clock, L_clock, n74161_bus_2_tc, n74161_bus_3_tc, n74161_bus_4_tc, n74191_bus_2_nrco,
       n74191_bus_3_nrco, n74191_bus_4_nrco, nA_out, nALU_out, nand_1_out, nand_2_out, nand_3_out,
       nand_4_out, nB_out, nC_out, nCLOCK1, nCLOCK2, nH_out, nL_out, nMAR_H_load, nMAR_H_reg_load,
       nMAR_L_load, nMAR_L_reg_load, nor_2_out, nPC_H_out, nPC_L_out, nPC_MAR_transfer, nRESET, nSTK_CLK_EN,
       nSTK_H_out, nSTK_L_out, nSTK_MAR_transfer, or_1_out, or_2_out, STK_DOWN_nUP;
  wire [3:0] A_p, A_p_2, B_p, B_p_2, C_p, C_p_2, H_p, H_p_2, IR_p, IR_p_2, L_p, L_p_2, n74161_bus_1_q,
       n74161_bus_2_q, n74161_bus_3_q, n74161_bus_4_q, n74191_bus_1_q, n74191_bus_2_q, n74191_bus_3_q,
       n74191_bus_4_q, n74574_peek_1_p, n74574_peek_1_p_2;
  wire [7:0] cscvon8_alu_1_p2, cscvon8_alu_1_p4;
  wire [15:0] ADDRESS;

  Clock clock_1 (.out(clock_1_out));
  Clock_Phases clock_phases_1 (
    .CLOCK(clock_1_out), .CLOCK1(CLOCK1), .CLOCK2(CLOCK2), .nCLOCK1(nCLOCK1), .nCLOCK2(nCLOCK2));
  Hex_Digit_Display hex_digit_display_1 (.value(A_p_2));  // open: dp
  _74574_Peek A (.nOE(nA_out), .CLK(A_clock), .D(in_1), .Q(in_1), .P({A_p_2, A_p}));
  nor nor_1 (STK_DOWN_nUP, in_23, nor_2_out);
  nor nor_2 (nor_2_out, STK_DOWN_nUP, in_25);
  nor nor_3 (nSTK_CLK_EN, in_25, in_23);
  Hex_Digit_Display hex_digit_display_2 (.value(A_p));  // open: dp
  // IC_74377 ic_74377_1: pin names not known; wires that end beside it: A_clock, 1'b0
  Hex_Digit_Display hex_digit_display_3 (.value(B_p_2));  // open: dp
  _74574_Peek B (.nOE(nB_out), .CLK(B_clock), .D(in_1), .Q(in_1), .P({B_p_2, B_p}));
  // CSCvon8_ALU cscvon8_alu_1: pin names not known; wires that end beside it: in_1, cscvon8_alu_1_p2, Function, cscvon8_alu_1_p4, FLAGS__DNZOC, 1'b1
  nand nand_1 (nand_1_out, in_27, CLOCK2);
  nand nand_2 (nand_2_out, CLOCK2, in_29);
  Hex_Digit_Display hex_digit_display_4 (.value(in_1[7:4]));  // open: dp
  Hex_Digit_Display hex_digit_display_5 (.value(B_p));  // open: dp
  Hex_Digit_Display hex_digit_display_6 (.value(n74574_peek_1_p_2));  // open: dp
  _74574_Peek u_74574_peek_1 (
    .nOE(nALU_out), .CLK(ALU_clock), .D(cscvon8_alu_1_p4), .Q(in_1), .P({n74574_peek_1_p_2, n74574_peek_1_p}));
  Hex_Digit_Display hex_digit_display_7 (.value(n74191_bus_1_q));  // open: dp
  Hex_Digit_Display hex_digit_display_8 (.value(n74191_bus_2_q));  // open: dp
  _74191_Bus u_74191_bus_1 (
    .nU_D(STK_DOWN_nUP), .CK(n74191_bus_2_nrco), .nCTEN(nSTK_CLK_EN), .nPL(nand_1_out), .Q(n74191_bus_1_q),
    .D(in_1[7:4]));  // open: TC, nRCO
  Hex_Digit_Display hex_digit_display_9 (.value(in_1[3:0]));  // open: dp
  Hex_Digit_Display hex_digit_display_10 (.value(C_p_2));  // open: dp
  _74574_Peek C (.nOE(nC_out), .CLK(C_clock), .D(in_1), .Q(in_1), .P({C_p_2, C_p}));
  Hex_Digit_Display hex_digit_display_11 (.value(n74574_peek_1_p));  // open: dp
  Hex_Digit_Display hex_digit_display_12 (.value(n74191_bus_3_q));  // open: dp
  Hex_Digit_Display hex_digit_display_13 (.value(n74191_bus_4_q));  // open: dp
  Hex_Digit_Display hex_digit_display_14 (.value(C_p));  // open: dp
  _74191_Bus u_74191_bus_2 (
    .nU_D(STK_DOWN_nUP), .CK(n74191_bus_3_nrco), .nCTEN(nSTK_CLK_EN), .nPL(nand_1_out),
    .nRCO(n74191_bus_2_nrco), .Q(n74191_bus_2_q), .D(in_1[3:0]));  // open: TC
  Hex_Digit_Display hex_digit_display_15 (.value(H_p_2));  // open: dp
  _74574_Peek H (.nOE(nH_out), .CLK(H_clock), .D(in_1), .Q(in_1), .P({H_p_2, H_p}));
  or or_1 (or_1_out, in_17, in_19);
  _74191_Bus u_74191_bus_3 (
    .nU_D(STK_DOWN_nUP), .CK(n74191_bus_4_nrco), .nCTEN(nSTK_CLK_EN), .nPL(nand_2_out),
    .nRCO(n74191_bus_3_nrco), .Q(n74191_bus_3_q), .D(in_1[7:4]));  // open: TC
  Hex_Digit_Display hex_digit_display_16 (.value(H_p));  // open: dp
  and and_1 (and_1_out, or_1_out, CLOCK2);
  nand nand_3 (nand_3_out, in_19, CLOCK1);
  Hex_Digit_Display hex_digit_display_17 (.value(n74161_bus_1_q));  // open: dp
  Hex_Digit_Display hex_digit_display_18 (.value(n74161_bus_2_q));  // open: dp
  _74244_Bus u_74244_bus_1 (.A({n74191_bus_3_q, n74191_bus_4_q}), .nOE(nSTK_L_out), .B(in_1));
  _74244_Bus u_74244_bus_2 (.A({n74191_bus_1_q, n74191_bus_2_q}), .nOE(nSTK_H_out), .B(in_1));
  _74244_Bus u_74244_bus_3 (.A({n74191_bus_3_q, n74191_bus_4_q}), .nOE(nSTK_MAR_transfer), .B(ADDRESS[7:0]));
  _74244_Bus u_74244_bus_4 (.A({n74191_bus_1_q, n74191_bus_2_q}), .nOE(nSTK_MAR_transfer), .B(ADDRESS[15:8]));
  Hex_Digit_Display hex_digit_display_19 (.value(L_p_2));  // open: dp
  _74574_Peek L (.nOE(nL_out), .CLK(L_clock), .D(in_1), .Q(in_1), .P({L_p_2, L_p}));
  _74161_Bus u_74161_bus_1 (
    .CLK(and_1_out), .nCLR(nRESET), .nPE(nand_3_out), .CEP(n74161_bus_2_tc), .CET(n74161_bus_2_tc),
    .D(in_1[7:4]), .Q(n74161_bus_1_q));  // open: TC
  Hex_Digit_Display hex_digit_display_20 (.value(n74161_bus_3_q));  // open: dp
  Hex_Digit_Display hex_digit_display_21 (.value(n74161_bus_4_q));  // open: dp
  _74191_Bus u_74191_bus_4 (
    .nU_D(STK_DOWN_nUP), .CK(CLOCK2), .nCTEN(nSTK_CLK_EN), .nPL(nand_2_out), .nRCO(n74191_bus_4_nrco),
    .Q(n74191_bus_4_q), .D(in_1[3:0]));  // open: TC
  Hex_Digit_Display hex_digit_display_22 (.value(L_p));  // open: dp
  Hex_Digit_Display hex_digit_display_23 (.value(IR_p_2));  // open: dp
  _74574_Peek IR (.nOE(1'b0), .CLK(IR_clock), .P({IR_p_2, IR_p}));  // open: D, Q
  _74161_Bus u_74161_bus_2 (
    .CLK(and_1_out), .nCLR(nRESET), .nPE(nand_3_out), .CEP(n74161_bus_3_tc), .CET(n74161_bus_3_tc),
    .D(in_1[3:0]), .Q(n74161_bus_2_q), .TC(n74161_bus_2_tc));
  Hex_Digit_Display hex_digit_display_24 (.value(IR_p));  // open: dp
  _74244_Bus u_74244_bus_5 (.A({n74161_bus_3_q, n74161_bus_4_q}), .nOE(nPC_L_out), .B(in_1));
  _74244_Bus u_74244_bus_6 (.A({n74161_bus_1_q, n74161_bus_2_q}), .nOE(nPC_H_out), .B(in_1));
  _74244_Bus u_74244_bus_7 (.A({n74161_bus_3_q, n74161_bus_4_q}), .nOE(nPC_MAR_transfer), .B(ADDRESS[7:0]));
  _74244_Bus u_74244_bus_8 (.A({n74161_bus_1_q, n74161_bus_2_q}), .nOE(nPC_MAR_transfer), .B(ADDRESS[15:8]));
  _74161_Bus u_74161_bus_3 (
    .CLK(and_5_out), .nCLR(nRESET), .nPE(nand_4_out), .CEP(n74161_bus_4_tc), .CET(n74161_bus_4_tc),
    .D(in_1[7:4]), .Q(n74161_bus_3_q), .TC(n74161_bus_3_tc));
  _74244_Bus u_74244_bus_9 (.A(in_1), .nOE(nMAR_L_load), .B(ADDRESS[7:0]));
  _74244_Bus u_74244_bus_10 (.A(in_1), .nOE(nMAR_H_load), .B(ADDRESS[15:8]));
  and and_2 (nMAR_H_reg_load, nMAR_H_load, and_3_out);
  and and_3 (and_3_out, nPC_MAR_transfer, nSTK_MAR_transfer);
  and and_4 (nMAR_L_reg_load, and_3_out, nMAR_L_load);
  Pull_Resistor pull_resistor_1 (.node(B_clock));
  Pull_Resistor pull_resistor_2 (.node(H_clock));
  Pull_Resistor pull_resistor_3 (.node(A_clock));
  Pull_Resistor pull_resistor_4 (.node(C_clock));
  // IC_74244 ic_74244_1: pin names not known; wires that end beside it: in_3, in_5, in_7, in_9, in_11, in_13, in_15, CLOCK2, CLOCK2, A_clock, B_clock, C_clock, H_clock, L_clock, IR_clock, ALU_clock
  _74161_Bus u_74161_bus_4 (
    .CLK(and_5_out), .nCLR(nRESET), .nPE(nand_4_out), .CEP(1'b1), .CET(1'b1), .D(in_1[3:0]),
    .Q(n74161_bus_4_q), .TC(n74161_bus_4_tc));
  Pull_Resistor pull_resistor_5 (.node(IR_clock));
  Pull_Resistor pull_resistor_6 (.node(L_clock));
  Pull_Resistor pull_resistor_7 (.node(ALU_clock));
  and and_5 (and_5_out, or_2_out, CLOCK2);
  nand nand_4 (nand_4_out, in_21, CLOCK1);
  _74377_Bus u_74377_bus_1 (.D(ADDRESS[7:0]), .CLK(nCLOCK2), .nCE(nMAR_L_reg_load));  // open: Q
  _74377_Bus u_74377_bus_2 (.D(ADDRESS[15:8]), .CLK(nCLOCK2), .nCE(nMAR_H_reg_load));  // open: Q
  or or_2 (or_2_out, in_17, in_21);
  not not_1 (nA_out, in_4);
  not not_2 (nB_out, in_6);
  not not_3 (nC_out, in_8);
  not not_4 (nH_out, in_10);
  not not_5 (nL_out, in_12);
  not not_6 (nALU_out, in_14);
  not not_7 (nRESET, in_16);
  not not_8 (nPC_H_out, in_18);
  not not_9 (nPC_L_out, in_20);
  not not_10 (nSTK_H_out, in_22);
  not not_11 (nSTK_L_out, in_24);
  not not_12 (nPC_MAR_transfer, in_26);
  not not_13 (nSTK_MAR_transfer, in_28);
  not not_14 (nMAR_H_load, in_30);
  not not_15 (nMAR_L_load, in_32);

  // Other names for the same wires on the sheet: A_load = in_3; ALU_load = in_15; B_load = in_5; C_load = in_7;
  //   DATA[7:0] = in_1; H_load = in_9; IR_load = in_13; L_load = in_11; PC_H_load = in_19; PC_inc = in_17;
  //   PC_L_load = in_21; STK_dec = in_25; STK_H_load = in_27; STK_inc = in_23; STK_L_load = in_29

  // Notes on the sheet:
  //   STACK POINTER
  //   ALU
  //   STK_H
  //   STK_L
  //   PC_H
  //   PC_H
  //   PC_L
  //   PROGRAM COUNTER
  //   PC_L
  //   Combine PC with SP on PCB, replace AND gates with buffer
  //   MEMORY ACCESS REGISTER
endmodule

// CLOCK
module Clock_Phases (
  input  CLOCK,
  output CLOCK1,
  output CLOCK2,
  output nCLOCK1,
  output nCLOCK2
);

  wire and_1_out, and_2_out, d_ff_3_q, d_ff_4_q;

  D_Flip_Flop d_ff_1 (.clk(CLOCK), .D(CLOCK), .Q(CLOCK1), .reset(and_1_out));  // open: Qn, preset, en
  D_Flip_Flop d_ff_2 (.clk(CLOCK), .D(CLOCK1), .Q(CLOCK2), .reset(and_2_out));  // open: Qn, preset, en
  not not_1 (nCLOCK1, CLOCK1);
  D_Flip_Flop d_ff_3 (.clk(CLOCK), .D(CLOCK2), .Q(d_ff_3_q), .reset(and_2_out));  // open: Qn, preset, en
  not not_2 (nCLOCK2, CLOCK2);
  and and_1 (and_1_out, CLOCK, d_ff_3_q);
  and and_2 (and_2_out, CLOCK, d_ff_4_q);
  D_Flip_Flop d_ff_4 (.clk(CLOCK), .D(d_ff_3_q), .Q(d_ff_4_q), .reset(and_2_out));  // open: Qn, preset, en
endmodule

module LCD_Decoder (
  input  [7:0] DATA,
  input  CLOCK,
  input  nLOAD,
  output RESET,
  output [15:0] COLOR,
  output LCD_CLOCK,
  output [6:0] X_COORD,
  output [6:0] Y_COORD
);

  wire and_1_out, and_3_out, dip_7474_1_p4, n74191_1_p13, n74191_1_p14, n74191_1_p15, n74191_1_p16,
       n74191_2_p13, n74191_3_p13, n74191_3_p14, nand_1_out, not_1_out, not_3_out, not_4_out, RESET_t;
  wire [7:5] ic_74377_1_p16;

  Pull_Resistor pull_resistor_1 (.node(DATA[0]));
  not not_1 (not_1_out, CLOCK);
  // IC_74377 ic_74377_1: pin names not known; wires that end beside it: DATA[0], DATA[1], DATA[2], DATA[3], DATA[4], DATA[5], DATA[6], DATA[7], not_1_out, nLOAD, COLOR[5], COLOR[6], COLOR[7], COLOR[8], COLOR[9], ic_74377_1_p16[5], ic_74377_1_p16[6], ic_74377_1_p16[7]
  and and_1 (and_1_out, ic_74377_1_p16[7], ic_74377_1_p16[6], ic_74377_1_p16[5], COLOR[9], COLOR[8], COLOR[7], COLOR[6], COLOR[5]);
  not not_2 (RESET_t, RESET);
  and and_2 (RESET, and_1_out, not_3_out);
  not not_3 (not_3_out, nLOAD);
  nand nand_1 (nand_1_out, CLOCK, nLOAD);
  and and_3 (and_3_out, CLOCK, not_3_out);
  and and_4 (LCD_CLOCK, RESET_t, dip_7474_1_p4);
  not not_4 (not_4_out, dip_7474_1_p4);
  // DIP_7474 dip_7474_1: pin names not known; wires that end beside it: nand_1_out, and_3_out, and_3_out, dip_7474_1_p4
  // _74191 74191_1: pin names not known; wires that end beside it: 1'b0, not_4_out, 1'b0, RESET_t, X_COORD[0], 1'b0, X_COORD[1], 1'b0, X_COORD[2], 1'b0, X_COORD[3], 1'b0, n74191_1_p13, n74191_1_p14, n74191_1_p15, n74191_1_p16
  // _74191 74191_2: pin names not known; wires that end beside it: 1'b0, n74191_1_p13, 1'b0, RESET_t, X_COORD[4], 1'b0, Y_COORD[0], 1'b0, Y_COORD[1], 1'b0, Y_COORD[2], 1'b0, n74191_2_p13
  // _74191 74191_3: pin names not known; wires that end beside it: 1'b0, n74191_2_p13, 1'b0, RESET_t, Y_COORD[3], 1'b0, Y_COORD[4], 1'b0, n74191_1_p14, 1'b0, n74191_1_p15, 1'b0, n74191_3_p13, n74191_3_p14
  // _74191 74191_4: pin names not known; wires that end beside it: 1'b0, n74191_3_p13, 1'b0, RESET_t, n74191_1_p16, 1'b0, n74191_3_p14, 1'b0, 1'b0, 1'b0

  assign {COLOR[15:10], COLOR[4:0]} = {11{1'b0}};
  assign X_COORD[6:5] = 2'b00;
  assign Y_COORD[6:5] = 2'b00;
endmodule

// 74161
module _74161_Clockfix (
  input  CLK,
  input  nCLR,
  input  nPE,
  input  CEP,
  input  CET,
  input  D1,
  input  D2,
  input  D3,
  input  D4,
  output Q1,
  output Q2,
  output Q3,
  output Q4,
  output TC
);

  wire and_1_out, and_2_out, and_3_out, and_4_out, and_5_out, and_6_out, and_7_out, and_8_out, and_9_out,
       and_10_out, and_11_out, and_12_out, not_1_out, not_2_out, or_1_out, or_2_out, or_3_out, or_4_out,
       xor_1_out, xor_2_out, xor_3_out, xor_4_out;

  not not_1 (not_1_out, nCLR);
  and and_1 (and_1_out, nPE, CEP, CET);
  not not_2 (not_2_out, nPE);
  and and_2 (and_2_out, D1, not_2_out);
  and and_3 (and_3_out, Q1, nPE);
  and and_4 (and_4_out, D2, not_2_out);
  and and_5 (and_5_out, Q2, nPE);
  and and_6 (and_6_out, Q1, and_1_out);
  and and_7 (and_7_out, D3, not_2_out);
  and and_8 (and_8_out, Q3, nPE);
  and and_9 (and_9_out, Q2, Q1, and_1_out);
  and and_10 (and_10_out, D4, not_2_out);
  and and_11 (and_11_out, Q4, nPE);
  and and_12 (and_12_out, Q3, Q2, Q1, and_1_out);
  xor xor_1 (xor_1_out, and_3_out, and_1_out);
  xor xor_2 (xor_2_out, and_5_out, and_6_out);
  xor xor_3 (xor_3_out, and_8_out, and_9_out);
  xor xor_4 (xor_4_out, and_11_out, and_12_out);
  or or_1 (or_1_out, and_2_out, xor_1_out);
  or or_2 (or_2_out, and_4_out, xor_2_out);
  or or_3 (or_3_out, and_7_out, xor_3_out);
  or or_4 (or_4_out, and_10_out, xor_4_out);
  // D_Flip_Flop d_flip_flop_1: pin names not known; wires that end beside it: or_1_out, CLK, not_1_out, Q1
  // D_Flip_Flop d_flip_flop_2: pin names not known; wires that end beside it: or_2_out, CLK, not_1_out, Q2
  // D_Flip_Flop d_flip_flop_3: pin names not known; wires that end beside it: or_3_out, CLK, not_1_out, Q3
  // D_Flip_Flop d_flip_flop_4: pin names not known; wires that end beside it: or_4_out, CLK, not_1_out, Q4
  and and_13 (TC, Q4, Q3, Q2, Q1, CET);
endmodule

module _74574_Peek (
  input  nOE,
  input  CLK,
  input  [7:0] D,
  output [7:0] P,
  output [7:0] Q
);

  wire not_1_out;

  not not_1 (not_1_out, nOE);
  // D_Flip_Flop d_flip_flop_1: pin names not known; wires that end beside it: D[0], P[0]
  // D_Flip_Flop d_flip_flop_2: pin names not known; wires that end beside it: CLK, D[1], CLK, P[1]
  // D_Flip_Flop d_flip_flop_3: pin names not known; wires that end beside it: D[2], P[2]
  // D_Flip_Flop d_flip_flop_4: pin names not known; wires that end beside it: CLK, D[3], CLK, P[3]
  // D_Flip_Flop d_flip_flop_5: pin names not known; wires that end beside it: D[4], CLK, P[4]
  // D_Flip_Flop d_flip_flop_6: pin names not known; wires that end beside it: D[5], P[5]
  // D_Flip_Flop d_flip_flop_7: pin names not known; wires that end beside it: CLK, D[6], P[6]
  // D_Flip_Flop d_flip_flop_8: pin names not known; wires that end beside it: CLK, D[7], CLK, P[7]
  assign Q[0] = not_1_out ? P[0] : 1'bz;  // Controlled_Buffer controlled_buffer_1
  assign Q[1] = not_1_out ? P[1] : 1'bz;  // Controlled_Buffer controlled_buffer_2
  assign Q[2] = not_1_out ? P[2] : 1'bz;  // Controlled_Buffer controlled_buffer_3
  assign Q[3] = not_1_out ? P[3] : 1'bz;  // Controlled_Buffer controlled_buffer_4
  assign Q[4] = not_1_out ? P[4] : 1'bz;  // Controlled_Buffer controlled_buffer_5
  assign Q[5] = not_1_out ? P[5] : 1'bz;  // Controlled_Buffer controlled_buffer_6
  assign Q[6] = not_1_out ? P[6] : 1'bz;  // Controlled_Buffer controlled_buffer_7
  assign Q[7] = not_1_out ? P[7] : 1'bz;  // Controlled_Buffer controlled_buffer_8

  // Notes on the sheet:
  //   This is the 74x574 chip, but with a PEEK output that always outputs the value stored in ther register
endmodule

module _74161_Bus (
  input  CLK,
  input  nCLR,
  input  nPE,
  input  CEP,
  input  CET,
  input  [3:0] D,
  output [3:0] Q,
  output TC
);

  wire and_1_out, and_2_out, and_3_out, and_4_out, and_5_out, and_6_out, and_7_out, and_8_out, and_9_out,
       and_10_out, and_11_out, and_12_out, not_1_out, not_2_out, or_1_out, or_2_out, or_3_out, or_4_out,
       xor_1_out, xor_2_out, xor_3_out, xor_4_out;

  not not_1 (not_1_out, nCLR);
  and and_1 (and_1_out, nPE, CEP, CET);
  not not_2 (not_2_out, nPE);
  and and_2 (and_2_out, D[0], not_2_out);
  and and_3 (and_3_out, Q[0], nPE);
  and and_4 (and_4_out, D[1], not_2_out);
  and and_5 (and_5_out, Q[1], nPE);
  and and_6 (and_6_out, Q[0], and_1_out);
  and and_7 (and_7_out, D[2], not_2_out);
  and and_8 (and_8_out, Q[2], nPE);
  and and_9 (and_9_out, Q[1], Q[0], and_1_out);
  and and_10 (and_10_out, D[3], not_2_out);
  and and_11 (and_11_out, Q[3], nPE);
  and and_12 (and_12_out, Q[2], Q[1], Q[0], and_1_out);
  xor xor_1 (xor_1_out, and_3_out, and_1_out);
  xor xor_2 (xor_2_out, and_5_out, and_6_out);
  xor xor_3 (xor_3_out, and_8_out, and_9_out);
  xor xor_4 (xor_4_out, and_11_out, and_12_out);
  or or_1 (or_1_out, and_2_out, xor_1_out);
  or or_2 (or_2_out, and_4_out, xor_2_out);
  or or_3 (or_3_out, and_7_out, xor_3_out);
  or or_4 (or_4_out, and_10_out, xor_4_out);
  // D_Flip_Flop d_flip_flop_1: pin names not known; wires that end beside it: or_1_out, CLK, not_1_out, Q[0]
  // D_Flip_Flop d_flip_flop_2: pin names not known; wires that end beside it: or_2_out, CLK, not_1_out, Q[1]
  // D_Flip_Flop d_flip_flop_3: pin names not known; wires that end beside it: or_3_out, CLK, not_1_out, Q[2]
  // D_Flip_Flop d_flip_flop_4: pin names not known; wires that end beside it: or_4_out, CLK, not_1_out, Q[3]
  and and_13 (TC, Q[3], Q[2], Q[1], Q[0], CET);
endmodule

// 74244
module _74244_Bus (
  input  [7:0] A,
  input  nOE,
  output [7:0] B
);

  wire not_1_out, not_2_out;

  not not_1 (not_1_out, nOE);
  not not_2 (not_2_out, nOE);
  assign B[0] = not_1_out ? A[0] : 1'bz;  // Controlled_Buffer controlled_buffer_1
  assign B[1] = not_1_out ? A[1] : 1'bz;  // Controlled_Buffer controlled_buffer_2
  assign B[2] = not_1_out ? A[2] : 1'bz;  // Controlled_Buffer controlled_buffer_3
  assign B[3] = not_1_out ? A[3] : 1'bz;  // Controlled_Buffer controlled_buffer_4
  assign B[4] = not_2_out ? A[4] : 1'bz;  // Controlled_Buffer controlled_buffer_5
  assign B[5] = not_2_out ? A[5] : 1'bz;  // Controlled_Buffer controlled_buffer_6
  assign B[6] = not_2_out ? A[6] : 1'bz;  // Controlled_Buffer controlled_buffer_7
  assign B[7] = not_2_out ? A[7] : 1'bz;  // Controlled_Buffer controlled_buffer_8
endmodule

// 74191
module _74191_Bus (
  input  nU_D,
  input  CK,
  input  nCTEN,
  input  nPL,
  input  [3:0] D,
  output [3:0] Q,
  output TC,
  output nRCO
);

  wire and_1_out, and_2_out, and_3_out, and_4_out, and_5_out, and_6_out, and_7_out, and_8_out,
       jk_flipflop_1_p4, jk_flipflop_1_p5, jk_flipflop_1_p7, jk_flipflop_2_p4, jk_flipflop_2_p5,
       jk_flipflop_2_p7, jk_flipflop_3_p4, jk_flipflop_3_p7, jk_flipflop_4_p4, jk_flipflop_4_p5, nand_5_out,
       nor_1_out, not_1_out, not_2_out, not_3_out, not_4_out, not_5_out, not_6_out, not_7_out, not_8_out,
       not_9_out, or_1_out, or_2_out, or_3_out;

  not not_1 (not_1_out, nCTEN);
  not not_2 (not_2_out, nU_D);
  // JK_FlipFlop jk_flipflop_1: pin names not known; wires that end beside it: not_1_out, CK, not_1_out, jk_flipflop_1_p4, jk_flipflop_1_p5, Q[0], jk_flipflop_1_p7
  nand nand_1 (jk_flipflop_1_p5, not_3_out, not_4_out);
  not not_3 (not_3_out, nPL);
  not not_4 (not_4_out, D[0]);
  not not_5 (not_5_out, nU_D);
  nand nand_2 (jk_flipflop_1_p4, not_3_out, D[0]);
  and and_1 (and_1_out, Q[0], not_5_out, not_1_out);
  or or_1 (or_1_out, and_1_out, and_2_out);
  and and_2 (and_2_out, nU_D, jk_flipflop_1_p7, not_1_out);
  // JK_FlipFlop jk_flipflop_2: pin names not known; wires that end beside it: or_1_out, CK, or_1_out, jk_flipflop_2_p4, jk_flipflop_2_p5, Q[1], jk_flipflop_2_p7
  nand nand_3 (jk_flipflop_2_p5, not_3_out, not_6_out);
  nand nand_4 (jk_flipflop_2_p4, not_3_out, D[1]);
  not not_6 (not_6_out, D[1]);
  and and_3 (and_3_out, and_1_out, Q[1], not_1_out);
  and and_4 (and_4_out, and_2_out, jk_flipflop_2_p7, not_1_out);
  or or_2 (or_2_out, and_3_out, and_4_out);
  nand nand_5 (nand_5_out, not_3_out, not_7_out);
  // JK_FlipFlop jk_flipflop_3: pin names not known; wires that end beside it: or_2_out, CK, or_2_out, jk_flipflop_3_p4, nand_5_out, Q[2], jk_flipflop_3_p7
  nand nand_6 (jk_flipflop_3_p4, not_3_out, D[2]);
  not not_7 (not_7_out, D[2]);
  and and_5 (and_5_out, and_3_out, Q[2], not_1_out);
  and and_6 (and_6_out, and_4_out, jk_flipflop_3_p7, not_1_out);
  or or_3 (or_3_out, and_5_out, and_6_out);
  // JK_FlipFlop jk_flipflop_4: pin names not known; wires that end beside it: or_3_out, CK, or_3_out, jk_flipflop_4_p4, jk_flipflop_4_p5, Q[3]
  nand nand_7 (jk_flipflop_4_p5, not_3_out, not_8_out);
  not not_8 (not_8_out, D[3]);
  not not_9 (not_9_out, CK);
  nand nand_8 (jk_flipflop_4_p4, not_3_out, D[3]);
  Hex_Digit_Display hex_digit_display_1 (.value(Q));  // open: dp
  nor nor_1 (nor_1_out, Q[3], Q[2], Q[1], Q[0], not_2_out);
  and and_7 (and_7_out, not_2_out, Q[3], Q[2], Q[1], Q[0]);
  or or_4 (TC, nor_1_out, and_7_out);
  not not_10 (nRCO, and_8_out);
  and and_8 (and_8_out, TC, not_1_out, not_9_out);
endmodule

// 74377
module _74377_Bus (
  input  [7:0] D,
  input  CLK,
  input  nCE,
  output [7:0] Q
);

  wire and_1_out, not_1_out;

  not not_1 (not_1_out, nCE);
  and and_1 (and_1_out, CLK, not_1_out);
  // D_Flip_Flop d_flip_flop_1: pin names not known; wires that end beside it: D[0], and_1_out, Q[0]
  // D_Flip_Flop d_flip_flop_2: pin names not known; wires that end beside it: D[1], and_1_out, Q[1]
  // D_Flip_Flop d_flip_flop_3: pin names not known; wires that end beside it: D[2], and_1_out, Q[2]
  // D_Flip_Flop d_flip_flop_4: pin names not known; wires that end beside it: D[3], and_1_out, Q[3]
  // D_Flip_Flop d_flip_flop_5: pin names not known; wires that end beside it: D[4], and_1_out, Q[4]
  // D_Flip_Flop d_flip_flop_6: pin names not known; wires that end beside it: D[5], and_1_out, Q[5]
  // D_Flip_Flop d_flip_flop_7: pin names not known; wires that end beside it: D[6], and_1_out, Q[6]
  // D_Flip_Flop d_flip_flop_8: pin names not known; wires that end beside it: D[7], and_1_out, Q[7]
endmodule
